# Fritzing sketch ArduinoShield-MsgeqAudioToDMXWithScreen (saved by Fritzing 0.9.2b)
circuit board: 7.16272cm x 5.51388cm

parts:
  MSGEQ1 = MSGEQ7 DIP8 [chip_label=MSGEQ7 package="DIP (Dual Inline) [THT]"]
  TRS1 = Audio Jack (TRS) 3.5mm [package="PG203J [THT]"]
  R3 = Resistor [tolerance=±5% resistance=200k package=THT]
  C7 = Ceramic Capacitor [capacitance=33pF package="100 mil [THT, multilayer]"]
  C8 = Ceramic Capacitor [capacitance=0.1µF package="100 mil [THT, multilayer]"]
  C9 = Ceramic Capacitor [capacitance=0.1µF package="100 mil [THT, multilayer]"]
  C10 = Ceramic Capacitor [capacitance=100nF package="100 mil [THT, multilayer]"]
  TRS2 = Audio Jack (TRS) 3.5mm [package="4Ucon 08780 [THT]"]
  U1 = MAX485 [package=dil08]
  Grove1 = Grove OLED 128x96
  Composant3 = Arduino Prototyping Shield

nets:
  VCC: MSGEQ1.VDDA, R3.Pin_0, C8.1, U1.VCC, Grove1.VCC, Composant3.+5V, Composant3.N$70, Composant3.N$94, Composant3.N$117, Composant3.N$259, Composant3.N$273, Composant3.N$283, Composant3.N$314
  N1: MSGEQ1.VSSA, C8.0, Composant3.N$261, Composant3.N$277, Composant3.N$293
  N2: MSGEQ1.OUT, Composant3.A0, Composant3.N$262
  N3: MSGEQ1.STROBE, Composant3.D4, Composant3.N$263
  N4: MSGEQ1.IN, C10.0, Composant3.N$268, Composant3.N$269
  N5: MSGEQ1.GROUND, C9.0, Composant3.N$239
  N6: MSGEQ1.RESET, Composant3.D5, Composant3.N$236
  N7: MSGEQ1.CKIN, C7.1, Composant3.N$235
  GND: TRS1.Sleeve, C9.1, U1.GND, Grove1.GND, Composant3.GND, Composant3.N$53, Composant3.N$240, Composant3.N$377, Composant3.N$378
  N8: TRS1.Ring, Composant3.N$324, Composant3.N$325
  N9: TRS1.Tip, C10.1, Composant3.N$105, Composant3.N$305, Composant3.N$321
  N10: R3.Pin_1, C7.0, Composant3.N$231
  N11: TRS2.Sleeve, U1.B, Composant3.N$51
  N12: TRS2.Ring, U1.A, Composant3.N$50, Composant3.N$397
  N13: U1.RO, Composant3.D0(RX), Composant3.N$403
  N14: U1.RE, U1.DE, Composant3.D13, Composant3.N$402, Composant3.N$407, Composant3.N$408
  N15: U1.DI, Composant3.D1(TX), Composant3.N$410
  N16: Grove1.SDA, Composant3.SDA
  N17: Grove1.SCL, Composant3.SCL

custom parts:
  MSGEQ7 DIP8: MSGEQ7 DIP9=8
